// Logisim project Lab1.circ as structural Verilog: 1 circuit, main circuit main
module main (
);

  wire nand_1_out, nand_2_out, nand_3_out, nand_4_out, nand_5_out, nand_6_out, nand_7_out, nand_8_out,
       nand_9_out, nand_10_out, nand_11_out, nand_12_out, nand_13_out, nand_14_out, nand_15_out, nand_16_out,
       nand_17_out, nand_18_out, nand_19_out, undriven, undriven_2, undriven_3, undriven_4, undriven_5,
       undriven_6, undriven_7, undriven_8, undriven_9, undriven_10, undriven_11, undriven_12, undriven_13,
       undriven_14, undriven_15, undriven_16, undriven_17, undriven_18, undriven_19, undriven_20,
       undriven_21, undriven_22, xor_1_out, xor_2_out, xor_3_out, xor_4_out, xor_5_out, xor_6_out, xor_7_out,
       xor_8_out, xor_10_out, xor_11_out, xor_12_out, xor_13_out, xor_14_out, xor_15_out, xor_16_out,
       xor_17_out, xor_18_out, xor_19_out;

  nand nand_1 (nand_1_out, undriven_3, undriven_3);
  nand nand_2 (nand_2_out, undriven_4, undriven_4);
  nand nand_3 (nand_3_out, undriven, undriven);
  nand nand_4 (nand_4_out, undriven_2, undriven_2);
  xor xor_1 (xor_1_out, undriven_9, undriven_10);
  xor xor_2 (xor_2_out, undriven_11, undriven_11);
  xor xor_3 (xor_3_out, undriven_7, undriven_7);
  xor xor_4 (xor_4_out, undriven_8, undriven_8);
  xor xor_5 (xor_5_out, undriven_12, undriven_12);
  nand nand_5 (nand_5_out, undriven_5, undriven_6);
  nand nand_6 (nand_6_out, nand_1_out, nand_2_out);
  nand nand_7 (nand_7_out, nand_3_out, nand_4_out);
  nand nand_8 (nand_8_out, nand_5_out, nand_5_out);
  nand nand_9 (nand_9_out, nand_7_out, nand_7_out);
  xor xor_6 (xor_6_out, xor_1_out, xor_1_out);
  xor xor_7 (xor_7_out, xor_2_out, xor_3_out);
  xor xor_8 (xor_8_out, xor_4_out, xor_5_out);
  // XOR_Gate xor_9 has open pins: in0=xor_8_out, in1=xor_8_out, out=open
  nand nand_10 (nand_10_out, undriven_18, undriven_17);
  xor xor_10 (xor_10_out, undriven_13, undriven_13);
  xor xor_11 (xor_11_out, undriven_14, undriven_14);
  xor xor_12 (xor_12_out, undriven_15, undriven_16);
  nand nand_11 (nand_11_out, undriven_21, undriven_21);
  nand nand_12 (nand_12_out, undriven_19, undriven_19);
  nand nand_13 (nand_13_out, undriven_20, undriven_20);
  xor xor_13 (xor_13_out, undriven_22, undriven_22);
  xor xor_14 (xor_14_out, undriven_13, undriven_14);
  xor xor_15 (xor_15_out, xor_10_out, xor_11_out);
  nand nand_14 (nand_14_out, undriven_18, nand_10_out);
  nand nand_15 (nand_15_out, nand_10_out, undriven_17);
  nand nand_16 (nand_16_out, undriven_19, undriven_20);
  nand nand_17 (nand_17_out, nand_12_out, nand_13_out);
  xor xor_16 (xor_16_out, undriven_15, xor_12_out);
  xor xor_17 (xor_17_out, xor_12_out, undriven_16);
  nand nand_18 (nand_18_out, nand_14_out, nand_15_out);
  nand nand_19 (nand_19_out, nand_16_out, nand_17_out);
  xor xor_18 (xor_18_out, xor_14_out, xor_15_out);
  xor xor_19 (xor_19_out, xor_16_out, xor_17_out);

  // Notes on the sheet:
  //   A
  //   B
  //   A
  //   B
  //   A
  //   B
  //   A
  //   B
  //   A
  //   B
  //   A
  //   B
  //   Logic Gates using NAND gate only
  //   Logic Gates using NOR gates only
  //   AND Gate
  //   OR Gate
  //   NOR Gate
  //   OR Gate
  //   AND Gate
  //   NAND Gate
  //   A
  //   B
  //   A
  //   A
  //   B
  //   A
  //   B
  //   A
  //   B
  //   A
  //   NOT Gate
  //   XOR Gate
  //   XNOR Gate
  //   NOT Gate
  //   XOR Gate
  //   XNOR Gate
endmodule
