// Logisim project Lab2.circ as structural Verilog: 1 circuit, main circuit main
module main (
  input  in_1,
  input  in_2,
  input  in_3,
  input  A,
  input  B,
  input  CARRY_IN,
  input  in_7,
  input  in_8,
  input  in_9,
  input  in_10
);

  wire and_1_out, and_2_out, and_3_out, nand_1_out, nand_2_out, nand_3_out, nand_4_out, nand_5_out,
       nand_6_out, nand_7_out, nand_8_out, nand_9_out, nand_10_out, nand_11_out, nand_12_out, nand_13_out,
       nand_14_out, or_1_out, xor_1_out, xor_2_out, xor_3_out;

  xor xor_1 (xor_1_out, in_1, in_2);
  nand nand_1 (nand_1_out, A, B);
  xor xor_2 (xor_2_out, in_7, in_9);
  LED led_1 (.in(xor_2_out));
  // AND_Gate and_1 has open pins: out=and_1_out
  // AND_Gate and_2 has open pins: out=and_2_out
  // AND_Gate and_3 has open pins: out=and_3_out
  nand nand_2 (nand_2_out, A, nand_1_out);
  nand nand_3 (nand_3_out, nand_1_out, B);
  LED led_2 (.in(and_1_out));
  LED led_3 (.in(xor_3_out));
  xor xor_3 (xor_3_out, xor_1_out, in_3);
  nand nand_4 (nand_4_out, nand_2_out, nand_3_out);
  LED led_4 (.in(or_1_out));
  or or_1 (or_1_out, and_2_out, and_3_out);
  nand nand_5 (nand_5_out, nand_4_out, CARRY_IN);
  nand nand_6 (nand_6_out, in_8, in_10);
  nand nand_7 (nand_7_out, nand_4_out, nand_5_out);
  nand nand_8 (nand_8_out, nand_5_out, CARRY_IN);
  nand nand_9 (nand_9_out, in_8, nand_6_out);
  nand nand_10 (nand_10_out, nand_6_out, in_10);
  nand nand_11 (nand_11_out, nand_6_out, nand_6_out);
  nand nand_12 (nand_12_out, nand_7_out, nand_8_out);
  nand nand_13 (nand_13_out, nand_1_out, nand_5_out);
  nand nand_14 (nand_14_out, nand_9_out, nand_10_out);

  // Notes on the sheet:
  //   HALF ADDER
  //   Using NAND Gates
  //   FULL ADDER
  //   Using NAND Gates
  //   SUM
  //   CARRY
  //   CARRY OUT
  //   SUM
endmodule
