// Logisim project Lab3.circ as structural Verilog: 1 circuit, main circuit main
module main (
  input  S0,
  input  S1,
  input  S2,
  input  D0,
  input  D1,
  input  D2,
  input  D3,
  input  D4,
  input  D5,
  input  D6,
  input  D7,
  input  G0,
  input  G1,
  input  G2,
  input  G3,
  input  G4,
  input  G5,
  input  G6
);

  wire AND_2_out, AND_3_out, AND_4_out, AND_5_out, AND_6_out, AND_7_out, AND_8_out, AND_out, not_1_out,
       not_2_out, not_3_out, or_2_out, or_3_out, or_4_out, OR_out;

  not not_1 (not_1_out, S0);
  not not_2 (not_2_out, S1);
  not not_3 (not_3_out, S2);
  and AND (AND_out, D0, not_1_out, not_2_out, not_3_out);
  and AND_2 (AND_2_out, D1, not_1_out, not_2_out, S2);
  and AND_3 (AND_3_out, D2, not_1_out, S1, not_3_out);
  and AND_4 (AND_4_out, D3, not_1_out, S1, S2);
  and AND_5 (AND_5_out, D4, S0, not_2_out, not_3_out);
  and AND_6 (AND_6_out, D5, S0, not_2_out, S2);
  and AND_7 (AND_7_out, D6, S0, S1, not_3_out);
  and AND_8 (AND_8_out, D7, S0, S1, S2);
  or OR (OR_out, AND_out, AND_2_out, AND_3_out, AND_4_out, AND_5_out, AND_6_out, AND_7_out, AND_8_out);
  or or_2 (or_2_out, G6, G5, G4, G3);
  or or_3 (or_3_out, G6, G5, G2, G1);
  or or_4 (or_4_out, G6, G4, G2, G0);

  // Notes on the sheet:
  //   8x1 MULTIPLEXER
  //   8:3 Encoder
  //   A2
  //   A1
  //   A0
  //   Y
endmodule
