// Logisim project Lab4.circ as structural Verilog: 1 circuit, main circuit main
module main (
  input  in_1,
  input  in_2,
  input  in_3,
  input  in_4,
  input  in_5,
  input  in_6,
  input  in_7,
  input  in_8,
  input  in_9
);

  wire and_1_out, and_2_out, and_3_out, and_4_out, and_5_out, and_6_out, and_7_out, and_8_out, or_1_out,
       or_2_out, or_3_out, or_4_out, xor_1_out, xor_2_out, xor_3_out, xor_4_out, xor_5_out, xor_6_out,
       xor_7_out, xor_8_out;

  xor xor_1 (xor_1_out, in_1, in_2);
  xor xor_2 (xor_2_out, in_4, in_5);
  xor xor_3 (xor_3_out, in_6, in_7);
  xor xor_4 (xor_4_out, in_8, in_9);
  // AND_Gate and_1 has open pins: out=and_1_out
  // AND_Gate and_2 has open pins: out=and_2_out
  // AND_Gate and_3 has open pins: out=and_3_out
  // AND_Gate and_4 has open pins: out=and_4_out
  // AND_Gate and_5 has open pins: out=and_5_out
  // AND_Gate and_6 has open pins: out=and_6_out
  // AND_Gate and_7 has open pins: out=and_7_out
  // AND_Gate and_8 has open pins: out=and_8_out
  xor xor_5 (xor_5_out, xor_1_out, in_3);
  xor xor_6 (xor_6_out, xor_2_out, or_1_out);
  xor xor_7 (xor_7_out, xor_3_out, or_2_out);
  xor xor_8 (xor_8_out, xor_4_out, or_3_out);
  // OR_Gate or_1 has open pins: out=or_1_out
  // OR_Gate or_2 has open pins: out=or_2_out
  // OR_Gate or_3 has open pins: out=or_3_out
  // OR_Gate or_4 has open pins: out=or_4_out
  LED led_1 (.in(xor_5_out));
  LED led_2 (.in(xor_6_out));
  LED led_3 (.in(xor_7_out));
  LED led_4 (.in(xor_8_out));
  LED led_5 (.in(or_4_out));

  // Notes on the sheet:
  //   4-bit Ripple Carry Adder
  //   S1
  //   S2
  //   S3
  //   S4
  //   CO
endmodule
