// Logisim project Lab7.circ as structural Verilog: 1 circuit, main circuit main
module main (
  input  [1:0] Select_Line
);

  wire multiplexer_1_out, multiplexer_2_out, multiplexer_3_out, multiplexer_4_out, undriven, undriven_2,
       undriven_3, undriven_4, undriven_5, undriven_6, undriven_7, undriven_8, undriven_9, undriven_10,
       undriven_11, undriven_12;
  wire [3:0] register_1_q, register_2_q, register_3_q, register_4_q;

  Multiplexer #(.select(2), .enable("false")) multiplexer_1 (
    .in0(register_1_q[3]), .in1(register_2_q[3]), .in2(register_3_q[3]), .in3(register_4_q[3]),
    .out(multiplexer_1_out), .sel(Select_Line));
  Register #(.width(4)) register_1 (.Q(register_1_q));  // open: D, en, clk, clr
  Multiplexer #(.select(2), .enable("false")) multiplexer_2 (
    .in0(undriven), .in1(undriven_2), .in2(undriven_3), .in3(undriven_4), .out(multiplexer_2_out),
    .sel(Select_Line));
  Register #(.width(4)) register_2 (.Q(register_2_q));  // open: D, en, clk, clr
  Multiplexer #(.select(2), .enable("false")) multiplexer_3 (
    .in0(undriven_5), .in1(undriven_6), .in2(undriven_7), .in3(undriven_8), .out(multiplexer_3_out),
    .sel(Select_Line));
  Register #(.width(4)) register_3 (.Q(register_3_q));  // open: D, en, clk, clr
  Multiplexer #(.select(2), .enable("false")) multiplexer_4 (
    .in0(undriven_9), .in1(undriven_10), .in2(undriven_11), .in3(undriven_12), .out(multiplexer_4_out),
    .sel(Select_Line));
  Register #(.width(4)) register_4 (.Q(register_4_q));  // open: D, en, clk, clr

  // Notes on the sheet:
  //   Register D
  //   Register C
  //   4 - bit common bus system
  //   Register B
  //   Register A
endmodule
